// Logisim project 16to1MUX.circ as structural Verilog: 1 circuit, main circuit main
module main (
  input  in_1,
  input  in_2,
  input  in_3,
  input  in_4,
  input  in_5,
  input  in_6,
  input  in_7,
  input  in_8,
  input  in_9,
  input  in_10,
  input  in_11,
  input  in_12,
  input  in_13,
  input  in_14,
  input  in_15,
  input  in_16,
  input  in_17,
  input  in_18,
  input  in_19,
  input  in_20,
  input  in_21,
  input  in_22,
  input  in_23,
  input  in_24,
  input  in_25,
  input  in_26,
  input  in_27,
  input  in_28,
  input  in_29,
  input  in_30,
  input  in_31,
  output out_32
);

  wire multiplexer_1_out, multiplexer_2_out, multiplexer_3_out, multiplexer_4_out, multiplexer_5_out,
       multiplexer_6_out, multiplexer_7_out, multiplexer_8_out, multiplexer_9_out, multiplexer_10_out,
       multiplexer_11_out, multiplexer_12_out, multiplexer_13_out, multiplexer_14_out;

  Multiplexer multiplexer_1 (.in0(in_1), .in1(in_2), .out(multiplexer_1_out), .sel(in_3));  // open: en
  Multiplexer multiplexer_2 (.in0(in_4), .in1(in_6), .out(multiplexer_2_out), .sel(in_7));  // open: en
  Multiplexer multiplexer_3 (.in0(in_8), .in1(in_9), .out(multiplexer_3_out), .sel(in_11));  // open: en
  Multiplexer multiplexer_4 (.in0(in_12), .in1(in_14), .out(multiplexer_4_out), .sel(in_15));  // open: en
  Multiplexer multiplexer_5 (.in0(in_17), .in1(in_18), .out(multiplexer_5_out), .sel(in_19));  // open: en
  Multiplexer multiplexer_6 (.in0(in_20), .in1(in_22), .out(multiplexer_6_out), .sel(in_23));  // open: en
  Multiplexer multiplexer_7 (.in0(in_24), .in1(in_25), .out(multiplexer_7_out), .sel(in_27));  // open: en
  Multiplexer multiplexer_8 (.in0(in_28), .in1(in_30), .out(multiplexer_8_out), .sel(in_31));  // open: en
  Multiplexer multiplexer_9 (
    .in0(multiplexer_1_out), .in1(multiplexer_2_out), .out(multiplexer_9_out), .sel(in_5));  // open: en
  Multiplexer multiplexer_10 (
    .in0(multiplexer_3_out), .in1(multiplexer_4_out), .out(multiplexer_10_out), .sel(in_13));  // open: en
  Multiplexer multiplexer_11 (
    .in0(multiplexer_5_out), .in1(multiplexer_6_out), .out(multiplexer_11_out), .sel(in_21));  // open: en
  Multiplexer multiplexer_12 (
    .in0(multiplexer_7_out), .in1(multiplexer_8_out), .out(multiplexer_12_out), .sel(in_29));  // open: en
  Multiplexer multiplexer_13 (
    .in0(multiplexer_9_out), .in1(multiplexer_10_out), .out(multiplexer_13_out), .sel(in_10));  // open: en
  Multiplexer multiplexer_14 (
    .in0(multiplexer_11_out), .in1(multiplexer_12_out), .out(multiplexer_14_out), .sel(in_26));  // open: en
  Multiplexer multiplexer_15 (
    .in0(multiplexer_13_out), .in1(multiplexer_14_out), .out(out_32), .sel(in_16));  // open: en
endmodule
