// Logisim project 16to1MUXusing2to1MUX.circ as structural Verilog: 1 circuit, main circuit main
module main (
  input  in_1,
  input  in_2,
  input  in_3,
  input  in_4,
  input  in_5,
  input  in_6,
  input  in_7,
  input  in_8,
  input  in_9,
  input  in_10,
  input  in_11,
  input  in_12,
  input  in_13,
  input  in_14,
  input  in_15,
  input  in_16,
  input  in_17,
  input  in_18,
  input  in_19,
  input  in_20,
  input  in_21,
  input  in_22,
  input  in_23,
  input  in_24,
  input  in_25,
  input  in_26,
  input  in_27,
  input  in_28,
  input  in_29,
  input  in_30,
  input  in_31,
  output out_32
);

  wire and_1_out, and_2_out, and_3_out, and_4_out, and_5_out, and_6_out, and_7_out, and_8_out, and_9_out,
       and_10_out, and_11_out, and_12_out, and_13_out, and_14_out, and_15_out, and_16_out, and_17_out,
       and_18_out, and_19_out, and_20_out, and_21_out, and_22_out, and_23_out, and_24_out, and_25_out,
       and_26_out, and_27_out, and_28_out, and_29_out, and_30_out, not_1_out, not_2_out, not_3_out,
       not_4_out, not_5_out, not_6_out, not_7_out, not_8_out, not_9_out, not_10_out, not_11_out, not_12_out,
       not_13_out, not_14_out, not_15_out, or_1_out, or_2_out, or_3_out, or_4_out, or_5_out, or_6_out,
       or_7_out, or_8_out, or_9_out, or_10_out, or_11_out, or_12_out, or_13_out, or_14_out;

  not not_1 (not_1_out, in_3);
  not not_2 (not_2_out, in_7);
  not not_3 (not_3_out, in_11);
  not not_4 (not_4_out, in_15);
  not not_5 (not_5_out, in_19);
  not not_6 (not_6_out, in_23);
  not not_7 (not_7_out, in_27);
  not not_8 (not_8_out, in_31);
  and and_1 (and_1_out, in_1, in_3);
  and and_2 (and_2_out, in_2, not_1_out);
  and and_3 (and_3_out, in_4, in_7);
  and and_4 (and_4_out, in_6, not_2_out);
  and and_5 (and_5_out, in_8, in_11);
  and and_6 (and_6_out, in_10, not_3_out);
  and and_7 (and_7_out, in_12, in_15);
  and and_8 (and_8_out, in_13, not_4_out);
  and and_9 (and_9_out, in_17, in_19);
  and and_10 (and_10_out, in_18, not_5_out);
  and and_11 (and_11_out, in_20, in_23);
  and and_12 (and_12_out, in_21, not_6_out);
  and and_13 (and_13_out, in_24, in_27);
  and and_14 (and_14_out, in_25, not_7_out);
  and and_15 (and_15_out, in_28, in_31);
  and and_16 (and_16_out, in_29, not_8_out);
  or or_1 (or_1_out, and_1_out, and_2_out);
  or or_2 (or_2_out, and_3_out, and_4_out);
  or or_3 (or_3_out, and_5_out, and_6_out);
  or or_4 (or_4_out, and_7_out, and_8_out);
  or or_5 (or_5_out, and_9_out, and_10_out);
  or or_6 (or_6_out, and_11_out, and_12_out);
  or or_7 (or_7_out, and_13_out, and_14_out);
  or or_8 (or_8_out, and_15_out, and_16_out);
  not not_9 (not_9_out, in_5);
  not not_10 (not_10_out, in_14);
  not not_11 (not_11_out, in_22);
  and and_17 (and_17_out, or_3_out, in_14);
  and and_18 (and_18_out, or_4_out, not_10_out);
  not not_12 (not_12_out, in_30);
  and and_19 (and_19_out, or_1_out, in_5);
  and and_20 (and_20_out, or_2_out, not_9_out);
  and and_21 (and_21_out, or_5_out, in_22);
  and and_22 (and_22_out, or_6_out, not_11_out);
  and and_23 (and_23_out, or_7_out, in_30);
  and and_24 (and_24_out, or_8_out, not_12_out);
  or or_9 (or_9_out, and_19_out, and_20_out);
  or or_10 (or_10_out, and_17_out, and_18_out);
  or or_11 (or_11_out, and_21_out, and_22_out);
  or or_12 (or_12_out, and_23_out, and_24_out);
  not not_13 (not_13_out, in_9);
  not not_14 (not_14_out, in_26);
  and and_25 (and_25_out, or_9_out, in_9);
  and and_26 (and_26_out, or_10_out, not_13_out);
  and and_27 (and_27_out, or_11_out, in_26);
  and and_28 (and_28_out, or_12_out, not_14_out);
  or or_13 (or_13_out, and_25_out, and_26_out);
  or or_14 (or_14_out, and_27_out, and_28_out);
  not not_15 (not_15_out, in_16);
  and and_29 (and_29_out, or_13_out, in_16);
  and and_30 (and_30_out, or_14_out, not_15_out);
  or or_15 (out_32, and_29_out, and_30_out);
endmodule
