// Logisim project 16to1from2to1.circ as structural Verilog: 1 circuit, main circuit main
module main (
  input  in_1,
  input  in_2,
  input  in_3,
  input  in_4,
  input  in_5,
  input  in_6,
  input  in_7,
  input  in_8,
  input  in_9,
  input  in_10,
  input  in_11,
  input  in_12,
  input  in_13,
  input  in_14,
  input  in_15,
  input  in_16,
  input  in_17,
  input  in_18,
  input  in_19,
  input  in_20,
  output out_21
);

  wire main_1_out_4, main_2_out_4, main_3_out_4, main_4_out_4, main_5_out_4, main_6_out_4, main_7_out_4,
       main_8_out_4, main_9_out_4, main_10_out_4, main_11_out_4, main_12_out_4, main_13_out_4, main_14_out_4;

  _2TO1multiplexer_main main_1 (.in_1(in_1), .in_2(in_20), .in_3(in_2), .out_4(main_1_out_4));
  _2TO1multiplexer_main main_2 (.in_1(in_3), .in_2(in_20), .in_3(in_4), .out_4(main_2_out_4));
  _2TO1multiplexer_main main_3 (.in_1(in_5), .in_2(in_20), .in_3(in_6), .out_4(main_3_out_4));
  _2TO1multiplexer_main main_4 (.in_1(in_7), .in_2(in_20), .in_3(in_8), .out_4(main_4_out_4));
  _2TO1multiplexer_main main_5 (.in_1(in_9), .in_2(in_20), .in_3(in_10), .out_4(main_5_out_4));
  _2TO1multiplexer_main main_6 (.in_1(in_11), .in_2(in_20), .in_3(in_12), .out_4(main_6_out_4));
  _2TO1multiplexer_main main_7 (.in_1(in_13), .in_2(in_20), .in_3(in_14), .out_4(main_7_out_4));
  _2TO1multiplexer_main main_8 (.in_1(in_15), .in_2(in_20), .in_3(in_16), .out_4(main_8_out_4));
  _2TO1multiplexer_main main_9 (.in_1(main_1_out_4), .in_2(in_17), .in_3(main_2_out_4), .out_4(main_9_out_4));
  _2TO1multiplexer_main main_10 (.in_1(main_3_out_4), .in_2(in_17), .in_3(main_4_out_4), .out_4(main_10_out_4));
  _2TO1multiplexer_main main_11 (.in_1(main_5_out_4), .in_2(in_17), .in_3(main_6_out_4), .out_4(main_11_out_4));
  _2TO1multiplexer_main main_12 (.in_1(main_7_out_4), .in_2(in_17), .in_3(main_8_out_4), .out_4(main_12_out_4));
  _2TO1multiplexer_main main_13 (.in_1(main_9_out_4), .in_2(in_18), .in_3(main_10_out_4), .out_4(main_13_out_4));
  _2TO1multiplexer_main main_14 (.in_1(main_11_out_4), .in_2(in_18), .in_3(main_12_out_4), .out_4(main_14_out_4));
  _2TO1multiplexer_main main_15 (.in_1(main_13_out_4), .in_2(in_19), .in_3(main_14_out_4), .out_4(out_21));
endmodule
