// Logisim project 4 bit subtractor.circ as structural Verilog: 1 circuit, main circuit main
module main (
  input  in_1,
  input  in_2,
  input  A,
  input  in_4,
  input  in_5,
  input  B,
  input  in_7,
  input  in_8,
  output out_9,
  output out_10,
  output out_11,
  output out_12,
  output out_13
);

  wire main_2_bout, main_3_bout, main_4_a_b_2;

  Full_Subtractor_main main_1 (.A(in_1), .B(in_5), .Bin(main_2_bout), .DIFFERENCE(out_10), .Bout(out_9));
  Full_Subtractor_main main_2 (.A(A), .B(B), .Bin(main_3_bout), .DIFFERENCE(out_11), .Bout(main_2_bout));
  Full_Subtractor_main main_3 (.A(in_4), .B(in_8), .Bin(main_4_a_b_2), .DIFFERENCE(out_12), .Bout(main_3_bout));
  Half_Subtractor_main main_4 (.A_B(out_13), .A_B_2(main_4_a_b_2), .A(in_7), .B(in_2));

  // Notes on the sheet:
  //     B3
  //   A3
  //                       FULL SUBTRACTOR
  //      B2
  //   A2
  //                       FULL SUBTRACTOR
  //   BORROW
  //   OUTPUT
  //   B1
  //                       FULL SUBTRACTOR
  //   A1
  //   B0 
  //   A0
  //                       HALF SUBTRACTOR
endmodule
