// Logisim project 4bit adder.circ as structural Verilog: 1 circuit, main circuit main
module main (
  input  in_1,
  input  in_2,
  input  in_3,
  input  in_4,
  input  in_5,
  input  B,
  input  in_7,
  input  in_8,
  output out_9,
  output out_10,
  output out_11,
  output out_12,
  output out_13
);

  wire main_2_c_out, main_3_c_out, main_4_a_b_2;

  Full_Adder_main main_1 (.A(in_1), .B(in_5), .C(main_2_c_out), .S(out_10), .C_OUT(out_9));
  Full_Adder_main main_2 (.A(in_3), .B(B), .C(main_3_c_out), .S(out_11), .C_OUT(main_2_c_out));
  Full_Adder_main main_3 (.A(in_4), .B(in_8), .C(main_4_a_b_2), .S(out_12), .C_OUT(main_3_c_out));
  Half_Adder_main main_4 (.A_B(out_13), .A_B_2(main_4_a_b_2), .in_1(in_7), .in_2(in_2));

  // Notes on the sheet:
  //   FULL ADDER
  //   C
  //   OUTPUT
  //   FULL ADDER
  //   A
  //   FULL ADDER
  //   HALF ADDER
endmodule
