// Logisim project 4bitadder.circ as structural Verilog: 1 circuit, main circuit main
module main (
  input  in_1,
  input  in_2,
  input  in_3,
  input  in_4,
  input  in_5,
  input  B,
  input  in_7,
  input  in_8,
  output out_9,
  output out_10,
  output out_11,
  output out_12,
  output out_13
);


  // Notes on the sheet:
  //   FULL ADDER
  //   C
  //   OUTPUT
  //   FULL ADDER
  //   FULL ADDER
  //   HALF ADDER
endmodule
