// Logisim project 7SegDisplay.circ as structural Verilog: 1 circuit, main circuit main
module main (
  input  D,
  input  C,
  input  B,
  input  A
);

  wire n7_segment_display_driver_1_a_2, n7_segment_display_driver_1_b_2, n7_segment_display_driver_1_c_2,
       n7_segment_display_driver_1_d_2, n7_segment_display_driver_1_e, n7_segment_display_driver_1_f,
       n7_segment_display_driver_1_g;

  _7_segment_display_driver u_7_segment_display_driver_1 (
    .D(D), .C(C), .B(B), .A(A), .a_2(n7_segment_display_driver_1_a_2), .b_2(n7_segment_display_driver_1_b_2),
    .c_2(n7_segment_display_driver_1_c_2), .d_2(n7_segment_display_driver_1_d_2),
    .e(n7_segment_display_driver_1_e), .f(n7_segment_display_driver_1_f), .g(n7_segment_display_driver_1_g));
  _7_Segment_Display u_7_segment_display_1 (
    .g(n7_segment_display_driver_1_g), .f(n7_segment_display_driver_1_f),
    .a(n7_segment_display_driver_1_a_2), .b(n7_segment_display_driver_1_b_2),
    .e(n7_segment_display_driver_1_e), .d(n7_segment_display_driver_1_d_2),
    .c(n7_segment_display_driver_1_c_2));  // open: dp
endmodule
