// Logisim project CPU.circ as structural Verilog: 3 circuits, main circuit ALU
module main (
  input  [7:0] Data,
  input  Store,
  input  Load,
  input  Add,
  input  Subtract
);

  wire clock_1_out, or_1_out;
  wire [7:0] AC_q, alu_1_output_lsb, controlled_buffer_1_out, controlled_buffer_2_out, mram_1_output;

  Clock clock_1 (.out(clock_1_out));
  mRAM mram_1 (.Clock(clock_1_out), .Store_if_0_Load_if_1(Load), .Data(Data), .Output(mram_1_output));
  or or_1 (or_1_out, Add, Subtract);
  assign controlled_buffer_1_out = or_1_out ? AC_q : 8'bz;  // Controlled_Buffer controlled_buffer_1
  assign controlled_buffer_2_out = or_1_out ? Data : 8'bz;  // Controlled_Buffer controlled_buffer_2
  ALU alu_1 (
    .Subtract(Subtract), .Input_2(controlled_buffer_2_out), .Input_1(controlled_buffer_1_out),
    .Output_LSB(alu_1_output_lsb));  // open: Output_MSB
  assign mram_1_output = or_1_out ? alu_1_output_lsb : 8'bz;  // Controlled_Buffer controlled_buffer_3
  Register AC (.D(mram_1_output), .en(1'b1), .Q(AC_q), .clk(clock_1_out));  // open: clr
  Hex_Digit_Display hex_digit_display_1 (.value(AC_q[7:4]));  // open: dp
  Hex_Digit_Display hex_digit_display_2 (.value(AC_q[3:0]));  // open: dp
endmodule

module ALU (
  input  Subtract,
  input  [7:0] Input_1,
  input  [7:0] Input_2,
  output [7:0] Output_LSB,
  output [3:0] Output_MSB
);

  wire adder_1_cout, subtractor_1_bout;
  wire [7:0] adder_1_out, multiplexer_1_out, subtractor_1_out;

  Multiplexer #(.width(8), .enable("false")) multiplexer_1 (
    .in0(Input_2), .in1(Input_2), .out(multiplexer_1_out), .sel(Subtract));
  Adder adder_1 (.a(Input_1), .b(multiplexer_1_out), .out(adder_1_out), .cout(adder_1_cout));  // open: cin
  Multiplexer #(.width(8), .enable("false")) multiplexer_2 (
    .in0(adder_1_out), .in1(subtractor_1_out), .out(Output_LSB), .sel(Subtract));
  Subtractor subtractor_1 (
    .a(Input_1), .b(multiplexer_1_out), .out(subtractor_1_out), .bout(subtractor_1_bout));  // open: bin
  Multiplexer #(.enable("false")) multiplexer_3 (
    .in0(adder_1_cout), .in1(subtractor_1_bout), .out(Output_MSB[0]), .sel(Subtract));

  assign Output_MSB[3:1] = 3'b000;
endmodule

module mRAM (
  input  [7:0] Data,
  input  Clock,
  input  Store_if_0_Load_if_1,
  output [7:0] Output
);

  wire not_1_out, pull_resistor_1_node, pull_resistor_2_node;
  wire [7:0] ram_1_data;

  Pull_Resistor #(.pull(1)) pull_resistor_1 (.node(pull_resistor_1_node));
  RAM #(.addrWidth(2)) ram_1 (
    .addr(2'b11), .data(ram_1_data), .sel(pull_resistor_1_node), .clk(Clock), .ld(Store_if_0_Load_if_1),
    .clr(pull_resistor_2_node));
  Pull_Resistor pull_resistor_2 (.node(pull_resistor_2_node));
  assign ram_1_data = not_1_out ? Data : 8'bz;  // Controlled_Buffer controlled_buffer_1
  not not_1 (not_1_out, Store_if_0_Load_if_1);
  assign Output = Store_if_0_Load_if_1 ? ram_1_data : 8'bz;  // Controlled_Buffer controlled_buffer_2
endmodule
