// Logisim project Half Adder.circ as structural Verilog: 1 circuit, main circuit main
module main (
  input  in_1,
  input  in_2,
  output A_B,
  output A_B_2
);

  xor xor_1 (A_B, in_2, in_1);
  and and_1 (A_B_2, in_2, in_1);

  // Notes on the sheet:
  //                                                  HALF ADDER
  //   SUM
  //     CARRY
endmodule
