// Logisim project Half Subtractor.circ as structural Verilog: 1 circuit, main circuit main
module main (
  input  A,
  input  B,
  output A_B,
  output A_B_2
);

  wire not_1_out;

  not not_1 (not_1_out, A);
  xor xor_1 (A_B, B, A);
  and and_1 (A_B_2, B, not_1_out);

  // Notes on the sheet:
  //                                                  HALF ADDER
  //   DIFFERENCE
  //     BORROW
endmodule
