// Logisim project Parity.circ as structural Verilog: 1 circuit, main circuit main
module main (
  input  A,
  input  B,
  input  C,
  input  A_2,
  input  B_2,
  input  C_2,
  input  P,
  output A_3,
  output B_3,
  output C_3,
  output P_2,
  output Cp
);

  wire xor_1_out, xor_2_out, xor_3_out;

  xor xor_1 (xor_1_out, A, B);
  xor xor_2 (xor_2_out, A_2, B_2);
  xor xor_3 (xor_3_out, C_2, P);
  xor xor_4 (P_2, xor_1_out, C);
  xor xor_5 (Cp, xor_2_out, xor_3_out);

  assign A_3 = A;
  assign B_3 = B;
  assign C_3 = C;

  // Notes on the sheet:
  //   3 BIT INPUT
  //   PARITY GENERATOR
  //   PARITY CHECK
endmodule
