// Logisim project RAM AND ROM.circ as structural Verilog: 1 circuit, main circuit main
module main (
  input  [15:0] in_1,
  input  [15:0] in_2,
  input  [31:0] in_3,
  input  Write,
  input  Read,
  output [31:0] out_6,
  output [31:0] out_7
);

  wire clock_1_out;

  Clock clock_1 (.out(clock_1_out));
  RAM #(.addrWidth(16), .dataWidth(32), .bus("separate")) ram_1 (
    .addr(in_2), .din(in_3), .data(out_7), .str(Write), .clk(clock_1_out), .ld(Read));  // open: sel, clr
  ROM #(.addrWidth(16), .dataWidth(32)) rom_1 (.addr(in_1), .data(out_6));  // open: sel

  // Notes on the sheet:
  //   Address Bus
  //   Data Bus
  //   RAM
  //   Output
  //   ROM
  //   contents of rom_1 (hex, n*v repeats v):
  //   0 2 216*0 11
endmodule
