// Logisim project Right Shift.circ as structural Verilog: 1 circuit, main circuit main
module main (
  input  Serial_Input,
  output out_2,
  output out_3,
  output out_4,
  output out_5
);

  wire clock_1_out;

  Clock clock_1 (.out(clock_1_out));
  D_Flip_Flop d_ff_1 (.clk(clock_1_out), .D(Serial_Input), .Q(out_2));  // open: Qn, preset, en, reset
  D_Flip_Flop d_ff_2 (.clk(clock_1_out), .D(out_2), .Q(out_3));  // open: Qn, preset, en, reset
  D_Flip_Flop d_ff_3 (.clk(clock_1_out), .D(out_3), .Q(out_4));  // open: Qn, preset, en, reset
  D_Flip_Flop d_ff_4 (.clk(clock_1_out), .D(out_4), .Q(out_5));  // open: Qn, preset, en, reset
endmodule
