// Logisim project SR-flip-flop.circ as structural Verilog: 1 circuit, main circuit main
module main (
  input  S,
  input  R,
  output out_3,
  output out_4
);

  wire clock_1_out, nand_1_out, nand_2_out;

  Clock clock_1 (.out(clock_1_out));
  nand nand_1 (nand_1_out, S, clock_1_out);
  nand nand_2 (nand_2_out, clock_1_out, R);
  nand nand_3 (out_3, nand_1_out, out_4);
  nand nand_4 (out_4, out_3, nand_2_out);

  // Notes on the sheet:
  //   Set
  //   Clock
  //   Reset
  //   SR FLIP FLOP
endmodule
