// Logisim project T.circ as structural Verilog: 1 circuit, main circuit main
module main (
  input  T,
  input  C,
  output Q,
  output nQ
);

  wire nand_1_out, nand_2_out;

  nand nand_1 (nand_1_out, nQ, T, C);
  nand nand_2 (nand_2_out, C, T, Q);
  nand nand_3 (Q, nand_1_out, nQ);
  nand nand_4 (nQ, Q, nand_2_out);
endmodule
