// Logisim project fullbitaddersubtractor.circ as structural Verilog: 1 circuit, main circuit main
module main (
  input  in_1,
  input  in_2,
  input  in_3,
  input  in_4,
  input  in_5,
  input  in_6,
  input  in_7,
  input  A0,
  input  in_9,
  output out_10,
  output out_11,
  output out_12,
  output out_13,
  output out_14
);

  wire main_2_c_out, main_3_c_out, main_4_c_out, xor_1_out, xor_2_out, xor_3_out, xor_4_out;

  xor xor_1 (xor_1_out, in_1, in_9);
  Full_Adder_main main_1 (.A(in_2), .B(xor_1_out), .C(main_2_c_out), .S(out_11), .C_OUT(out_10));
  xor xor_2 (xor_2_out, in_3, in_9);
  Full_Adder_main main_2 (.A(in_4), .B(xor_2_out), .C(main_3_c_out), .S(out_12), .C_OUT(main_2_c_out));
  xor xor_3 (xor_3_out, in_9, in_5);
  Full_Adder_main main_3 (.A(in_6), .B(xor_3_out), .C(main_4_c_out), .S(out_13), .C_OUT(main_3_c_out));
  xor xor_4 (xor_4_out, in_7, in_9);
  Full_Adder_main main_4 (.A(A0), .B(xor_4_out), .C(in_9), .S(out_14), .C_OUT(main_4_c_out));

  // Notes on the sheet:
  //   4 BIT ADDER SUBTRACTOR
endmodule
