// Logisim project halfadder.circ as structural Verilog: 1 circuit, main circuit main
module main (
  input  A,
  input  B,
  input  A_2,
  input  B_2,
  input  C,
  output CARRY,
  output SUM,
  output SUM_2,
  output CARRY_2
);

  wire nand_1_out, nand_2_out, nand_3_out, xor_1_out;

  xor xor_1 (xor_1_out, A_2, B_2);
  nand nand_1 (nand_1_out, A, B);
  xor xor_2 (SUM, A, B);
  nand nand_2 (nand_2_out, A_2, B_2);
  xor xor_3 (SUM_2, xor_1_out, C);
  nand nand_3 (nand_3_out, xor_1_out, C);
  nand nand_4 (CARRY, nand_1_out, nand_1_out);
  nand nand_5 (CARRY_2, nand_3_out, nand_2_out);

  // Notes on the sheet:
  //   HALF ADDER
  //   FULL ADDER
endmodule
