// Logisim project jk.circ as structural Verilog: 2 circuits, main circuit main
module main (
  input  S,
  input  C,
  input  R,
  output out_4,
  output out_5
);

  wire nand_1_out, nand_2_out;

  nand nand_1 (nand_1_out, out_5, S, C);
  nand nand_2 (nand_2_out, C, R, out_4);
  latch latch_1 (.in_1(nand_1_out), .in_2(nand_2_out), .out_3(out_4), .out_4(out_5));
endmodule

module latch (
  input  in_1,
  input  in_2,
  output out_3,
  output out_4
);

  nand nand_1 (out_3, in_1, out_4);
  nand nand_2 (out_4, out_3, in_2);
endmodule
