// Logisim project mod-10 counter.circ as structural Verilog: 1 circuit, main circuit main
module main (
  input  in_1,
  output out_2,
  output out_3,
  output out_4,
  output out_5,
  output out_6
);

  wire and_1_out, and_2_out, and_3_out, and_5_out, clock_1_out, not_1_out, not_2_out;

  and and_1 (and_1_out, in_1, out_2);
  and and_2 (and_2_out, and_1_out, out_3);
  and and_3 (and_3_out, and_2_out, out_4);
  Clock clock_1 (.out(clock_1_out));
  T_Flip_Flop t_ff_1 (.clk(clock_1_out), .T(in_1), .Q(out_2), .reset(and_5_out));  // open: Qn, preset, en
  T_Flip_Flop t_ff_2 (.clk(clock_1_out), .T(and_1_out), .Q(out_3), .reset(and_5_out));  // open: Qn, preset, en
  T_Flip_Flop t_ff_3 (.clk(clock_1_out), .T(and_2_out), .Q(out_4), .reset(and_5_out));  // open: Qn, preset, en
  T_Flip_Flop t_ff_4 (.clk(clock_1_out), .T(and_3_out), .Q(out_5), .reset(and_5_out));  // open: Qn, preset, en
  not not_1 (not_1_out, out_2);
  not not_2 (not_2_out, out_4);
  and and_4 (out_6, out_5, and_3_out);
  and and_5 (and_5_out, not_1_out, out_3, not_2_out, out_5);
endmodule
