// Logisim project sr-jk.circ as structural Verilog: 1 circuit, main circuit main
module main (
  input  S,
  input  C,
  input  R,
  input  J,
  input  C_2,
  input  k,
  output Q,
  output nQ,
  output out_9,
  output out_10
);

  wire nand_1_out, nand_2_out, nand_3_out, nand_4_out;

  nand nand_1 (nand_1_out, S, C);
  nand nand_2 (nand_2_out, C, R);
  nand nand_3 (nand_3_out, out_10, J, C_2);
  nand nand_4 (nand_4_out, C_2, k, out_9);
  nand nand_5 (out_9, nand_3_out, out_10);
  nand nand_6 (out_10, out_9, nand_4_out);
  nand nand_7 (Q, nand_1_out, nQ);
  nand nand_8 (nQ, Q, nand_2_out);
endmodule
